// Logisim project TallerLogica-Combinatorios.circ as structural Verilog: 11 circuits, main circuit sumador_simple
module sumador_simple (
  input  A,
  input  B,
  output S,
  output Cout
);

  and and_1 (Cout, A, B);
  xor xor_1 (S, A, B);
endmodule

module sumador_completo (
  input  Cin,
  input  A,
  input  B,
  output S,
  output Cout
);

  wire sumador_simple_1_cout, sumador_simple_1_s, sumador_simple_2_cout;

  sumador_simple sumador_simple_1 (.A(A), .B(B), .S(sumador_simple_1_s), .Cout(sumador_simple_1_cout));
  sumador_simple sumador_simple_2 (.A(Cin), .B(sumador_simple_1_s), .S(S), .Cout(sumador_simple_2_cout));
  xor xor_1 (Cout, sumador_simple_2_cout, sumador_simple_1_cout);
endmodule

module sumador_4 (
  input  Cin,
  input  [3:0] A,
  input  [3:0] B,
  output [3:0] S,
  output Cout
);

  wire sumador_completo_1_cout, sumador_completo_2_cout, sumador_completo_3_cout;

  sumador_completo sumador_completo_1 (.Cin(Cin), .A(A[0]), .B(B[0]), .S(S[0]), .Cout(sumador_completo_1_cout));
  sumador_completo sumador_completo_2 (
    .Cin(sumador_completo_1_cout), .A(A[1]), .B(B[1]), .S(S[1]), .Cout(sumador_completo_2_cout));
  sumador_completo sumador_completo_3 (
    .Cin(sumador_completo_2_cout), .A(A[2]), .B(B[2]), .S(S[2]), .Cout(sumador_completo_3_cout));
  sumador_completo sumador_completo_4 (.Cin(sumador_completo_3_cout), .A(A[3]), .B(B[3]), .S(S[3]), .Cout(Cout));
  Hex_Digit_Display hex_digit_display_1 (.value(S));  // open: dp
endmodule

module comparador_cero (
  input  [3:0] A,
  output Z
);

  wire nor_1_out, nor_2_out;

  nor nor_1 (nor_1_out, A[0], A[1]);
  nor nor_2 (nor_2_out, A[2], A[3]);
  and and_1 (Z, nor_1_out, nor_2_out);
endmodule

module sumador_flags (
  input  Cin,
  input  [3:0] A,
  input  [3:0] B,
  output V,
  output N,
  output [3:0] S,
  output Z,
  output C
);

  wire not_1_out, xor_1_out, xor_2_out;

  sumador_4 sumador_4_1 (.Cin(Cin), .A(A), .B(B), .S({N, S[2:0]}), .Cout(C));
  Hex_Digit_Display hex_digit_display_1 (.value({N, S[2:0]}));  // open: dp
  xor xor_1 (xor_1_out, A[3], B[3]);
  not not_1 (not_1_out, xor_1_out);
  xor xor_2 (xor_2_out, B[3], N);
  comparador_cero comparador_cero_1 (.A({N, S[2:0]}), .Z(Z));
  and and_1 (V, not_1_out, xor_2_out);

  assign S[3] = N;
endmodule

module incrementador_4 (
  input  [3:0] A,
  output [3:0] S
);

  Hex_Digit_Display hex_digit_display_1 (.value(S));  // open: dp
  sumador_4 sumador_4_1 (.Cin(1'b0), .A(A), .B(4'b0001), .S(S));  // open: Cout
endmodule

module inversor_4 (
  input  [3:0] A,
  input  INV,
  output [3:0] S
);

  wire not_1_out, not_2_out, not_3_out, not_4_out;
  wire [3:0] multiplexer_4_out;

  not not_1 (not_1_out, A[2]);
  Multiplexer multiplexer_1 (.in0(A[3]), .in1(not_2_out), .out(multiplexer_4_out[3]), .sel(INV));
  not not_2 (not_2_out, A[3]);
  not not_3 (not_3_out, A[0]);
  Multiplexer multiplexer_2 (.in0(A[1]), .in1(not_4_out), .out(multiplexer_4_out[1]), .sel(INV));
  not not_4 (not_4_out, A[1]);
  Multiplexer multiplexer_3 (.in0(A[2]), .in1(not_1_out), .out(multiplexer_4_out[2]), .sel(INV));
  Demultiplexer demultiplexer_1 ();  // open: out0, out1, in, sel
  Multiplexer multiplexer_4 (.in0(A[0]), .in1(not_3_out), .out(multiplexer_4_out[0]), .sel(INV));
  Hex_Digit_Display hex_digit_display_1 (.value(S));  // open: dp
  sumador_4 sumador_4_1 (.Cin(INV), .A(multiplexer_4_out), .B(4'b0000), .S(S));  // open: Cout

  // Notes on the sheet:
  //   Como hacemos para no usar sumador? 
endmodule

module ALU (
  input  [3:0] A,
  input  [3:0] B,
  input  [1:0] OP,
  output V,
  output N,
  output [3:0] S,
  output Z,
  output C
);

  wire sumador_flags_2_c;
  wire [3:0] a_and_b_1_s, a_or_b_1_s, inversor_4_1_s, multiplexer_1_out, sumador_flags_1_s, sumador_flags_2_s;
  wire [6:6] comparador_cero_1_z;
  wire [7:0] multiplexer_2_out, sumador_flags_1_v, sumador_flags_2_v;

  inversor_4 inversor_4_1 (.A(B), .INV(1'b1), .S(inversor_4_1_s));
  A_and_B a_and_b_1 (.A(A), .B(B), .S(a_and_b_1_s));
  A_or_B a_or_b_1 (.A(A), .B(B), .S(a_or_b_1_s));
  Multiplexer #(.width(4)) multiplexer_1 (.in0(a_and_b_1_s), .in1(a_or_b_1_s), .out(multiplexer_1_out), .sel(OP[0]));
  sumador_flags sumador_flags_1 (
    .Cin(1'b0), .A(A), .B(B), .V(sumador_flags_1_v[0]), .N(sumador_flags_1_v[1]), .S(sumador_flags_1_s),
    .Z(sumador_flags_1_v[6]), .C(sumador_flags_1_v[7]));
  sumador_flags sumador_flags_2 (
    .Cin(1'b0), .A(A), .B(inversor_4_1_s), .V(sumador_flags_2_v[0]), .N(sumador_flags_2_v[1]),
    .S(sumador_flags_2_s), .Z(sumador_flags_2_v[6]), .C(sumador_flags_2_c));
  not not_1 (sumador_flags_2_v[7], sumador_flags_2_c);
  comparador_cero comparador_cero_1 (.A(multiplexer_1_out), .Z(comparador_cero_1_z[6]));
  Multiplexer #(.width(8)) multiplexer_2 (
    .in0({sumador_flags_1_v[7:6], sumador_flags_1_s, sumador_flags_1_v[1:0]}),
    .in1({sumador_flags_2_v[7:6], sumador_flags_2_s, sumador_flags_2_v[1:0]}), .out(multiplexer_2_out),
    .sel(OP[0]));
  Multiplexer #(.width(8)) multiplexer_3 (
    .in0(multiplexer_2_out),
    .in1({1'b0, comparador_cero_1_z[6], multiplexer_1_out, multiplexer_1_out[3], 1'b0}),
    .out({C, Z, S, N, V}), .sel(OP[1]));
  Hex_Digit_Display hex_digit_display_1 (.value(S));  // open: dp
endmodule

module verificador (
  output [3:0] out_1,
  output [3:0] out_2,
  output [1:0] out_3,
  output halt,
  output N,
  output Z,
  output V,
  output C,
  output [3:0] res
);

  wire clock_1_out;

  Clock clock_1 (.out(clock_1_out));
  Counter #(.max('h3ff), .width(10)) counter_1 (
    .clk(clock_1_out), .carry(halt), .Q({out_3, out_2, out_1}));  // open: clr, load, up, count, D
  // ALU alu_1: pin names not known; wires that end beside it: out_1, out_2, out_3, N, Z, V, C, res
endmodule

module A_and_B (
  input  [3:0] A,
  input  [3:0] B,
  output [3:0] S
);

  and and_1 (S[0], A[0], B[0]);
  and and_2 (S[1], A[1], B[1]);
  and and_3 (S[2], A[2], B[2]);
  and and_4 (S[3], A[3], B[3]);
endmodule

module A_or_B (
  input  [3:0] A,
  input  [3:0] B,
  output [3:0] S
);

  or or_1 (S[0], A[0], B[0]);
  or or_2 (S[1], A[1], B[1]);
  or or_3 (S[2], A[2], B[2]);
  or or_4 (S[3], A[3], B[3]);
endmodule
